// Logisim project cpu.circ as structural Verilog: 1 circuit, main circuit cpu
module cpu (
  input  clk,
  input  [31:0] INSTRUCTION,
  input  [31:0] READ_DATA,
  output [31:0] WRITE_ADDRESS,
  output [31:0] PROGRAM_COUNTER,
  output [31:0] ra,
  output [31:0] sp,
  output [31:0] t0,
  output [31:0] t1,
  output [31:0] t2,
  output [31:0] s0,
  output [31:0] s1,
  output [31:0] a0,
  output [31:0] tohost,
  output [3:0] WRITE_ENABLE,
  output [31:0] WRITE_DATA
);

  wire ASel, BSel, regfile_1_p7, regfile_1_p8, regfile_1_p10, regfile_1_p20, regfile_1_p22, regfile_1_p24,
       regfile_1_p26, RegWEn;
  wire [2:0] control_logic_1_immsel;
  wire [3:0] ALUOp;
  wire [31:0] adder_1_out, ALURes, imm, multiplexer_1_out, regfile_1_p21;

  Adder #(.width(32)) adder_1 (.a(PROGRAM_COUNTER), .b(32'h4), .out(adder_1_out));  // open: cin, cout
  Register #(.width(32)) PC (.D(adder_1_out), .clk(clk), .Q(PROGRAM_COUNTER));  // open: en, clr
  control_logic control_logic_1 (
    .RegWEn(RegWEn), .ImmSel(control_logic_1_immsel), .ASel(ASel), .BSel(BSel), .ALUSel(ALUOp),
    .inst(INSTRUCTION));  // open: CSRWen, PCSel, BrUn, MemRW, WBSel, CSRSel, BrEq, BrLt
  imm_gen imm_gen_1 (.inst(INSTRUCTION), .ImmSel(control_logic_1_immsel), .imm(imm));
  // regfile regfile_1: pin names not known; wires that end beside it: INSTRUCTION[19:15], INSTRUCTION[24:20], INSTRUCTION[11:7], ALURes, RegWEn, clk, regfile_1_p7, regfile_1_p8, regfile_1_p8, regfile_1_p10, regfile_1_p10, ra, sp, t0, t1, t2, s0, s1, a0, regfile_1_p20, regfile_1_p21, regfile_1_p22, regfile_1_p22, regfile_1_p24, regfile_1_p24, regfile_1_p26
  // branch_comp branch_comp_1: pin names not known
  Multiplexer #(.enable("false"), .width(32)) multiplexer_1 (
    .in0(imm), .in1(regfile_1_p21), .out(multiplexer_1_out), .sel(BSel));
  // alu alu_1: pin names not known; wires that end beside it: regfile_1_p20, multiplexer_1_out, ALURes
  // csr csr_1: pin names not known; wires that end beside it: ALUOp, tohost

  // Notes on the sheet:
  //   Output to IMEM
  //   IMEM (do **NOT** move this)
  //   Inputs from IMEM
  //   Inputs/Outputs for testing. Do **NOT** move these.
  //   Outputs To DMEM
  //   DMEM (do **NOT** move this)
  //   Inputs From DMEM
endmodule
